# Fritzing sketch PROJETO (saved by Fritzing 0.9.3b)

parts:
  R1 = Rotary Potentiometer (Large) [maximum_resistance=100kΩ package=THT]
  R2 = Rotary Potentiometer (Large) [maximum_resistance=100kΩ package=THT]
  R3 = Rotary Potentiometer (Large) [maximum_resistance=100kΩ package=THT]
  LED1 = LED - 5mm [color="Red (633nm)" package="5 mm [THT]"]
  LED2 = LED - 5mm [color="Yellow (595nm)" package="5 mm [THT]"]
  LED3 = LED - 5mm [color="Green (570nm)" package="5 mm [THT]"]
  Componente1 = Arduino Nano (Rev3.0)
  J1 = Piezo Speaker

nets:
  N1: R1.leg1, R2.leg1, R3.leg1
  N2: R1.wiper, Componente1.A2
  N3: R2.wiper, Componente1.A1
  N4: R3.wiper, Componente1.A0
  N5: LED1.cathode, LED2.cathode, LED3.cathode, Componente1.GND, J1.pin1
  N6: LED1.anode, Componente1.D4
  N7: LED2.anode, Componente1.D3
  N8: LED3.anode, Componente1.D2
  N9: Componente1.D7, J1.pin2
